// Logisim project shifter_lab.circ as structural Verilog: 1 circuit, main circuit shifter8
module shifter8 (
  input  [3:0] SUCtrl,
  input  [7:0] X,
  output ZF,
  output SF,
  output Ouflw,
  output [7:0] R
);

  wire and_1_out, and_2_out, and_3_out, and_4_out, and_5_out, and_6_out, and_7_out, and_8_out,
       multiplexer_1_out, multiplexer_2_out, multiplexer_3_out, multiplexer_4_out, multiplexer_5_out,
       multiplexer_6_out, multiplexer_7_out, multiplexer_8_out, multiplexer_9_out, multiplexer_10_out,
       multiplexer_11_out, multiplexer_12_out, multiplexer_13_out, multiplexer_14_out, multiplexer_15_out,
       multiplexer_16_out, not_1_out, not_2_out, not_3_out, not_4_out, not_5_out, not_6_out, not_7_out,
       not_8_out, not_9_out, not_10_out;

  Multiplexer #(.select(2), .enable("false")) multiplexer_1 (
    .in0(multiplexer_2_out), .in1(1'b0), .in2(multiplexer_2_out), .in3(multiplexer_2_out),
    .out(multiplexer_1_out), .sel(SUCtrl[2:1]));
  Multiplexer #(.select(2)) multiplexer_2 (
    .in0(X[6]), .in1(X[3]), .in2(X[7]), .in3(X[7]), .out(multiplexer_2_out), .sel(SUCtrl[1:0]), .en(SUCtrl[3]));
  Multiplexer #(.select(2), .enable("false")) multiplexer_3 (
    .in0(multiplexer_4_out), .in1(multiplexer_2_out), .in2(multiplexer_4_out), .in3(multiplexer_2_out),
    .out(multiplexer_3_out), .sel(SUCtrl[2:1]));
  Multiplexer #(.select(2)) multiplexer_4 (
    .in0(X[5]), .in1(X[2]), .in2(X[6]), .in3(X[6]), .out(multiplexer_4_out), .sel(SUCtrl[1:0]), .en(SUCtrl[3]));
  Multiplexer #(.select(2)) multiplexer_5 (
    .in0(X[4]), .in1(X[1]), .in2(X[5]), .in3(X[5]), .out(multiplexer_5_out), .sel(SUCtrl[1:0]), .en(SUCtrl[3]));
  Multiplexer #(.select(2), .enable("false")) multiplexer_6 (
    .in0(multiplexer_5_out), .in1(multiplexer_4_out), .in2(multiplexer_5_out), .in3(multiplexer_4_out),
    .out(multiplexer_6_out), .sel(SUCtrl[2:1]));
  Multiplexer #(.select(2), .enable("false")) multiplexer_7 (
    .in0(multiplexer_8_out), .in1(multiplexer_5_out), .in2(multiplexer_8_out), .in3(multiplexer_5_out),
    .out(multiplexer_7_out), .sel(SUCtrl[2:1]));
  Multiplexer #(.select(2)) multiplexer_8 (
    .in0(X[3]), .in1(X[0]), .in2(X[4]), .in3(X[4]), .out(multiplexer_8_out), .sel(SUCtrl[1:0]), .en(SUCtrl[3]));
  Multiplexer #(.select(2), .enable("false")) multiplexer_9 (
    .in0(multiplexer_10_out), .in1(multiplexer_8_out), .in2(1'b0), .in3(multiplexer_8_out),
    .out(multiplexer_9_out), .sel(SUCtrl[2:1]));
  Multiplexer #(.select(2)) multiplexer_10 (
    .in0(X[2]), .in1(1'b0), .in2(X[3]), .in3(X[3]), .out(multiplexer_10_out), .sel(SUCtrl[1:0]),
    .en(SUCtrl[3]));
  Multiplexer #(.select(2), .enable("false")) multiplexer_11 (
    .in0(multiplexer_12_out), .in1(multiplexer_10_out), .in2(1'b0), .in3(multiplexer_10_out),
    .out(multiplexer_11_out), .sel(SUCtrl[2:1]));
  Multiplexer #(.select(2)) multiplexer_12 (
    .in0(X[1]), .in1(1'b0), .in2(X[2]), .in3(X[2]), .out(multiplexer_12_out), .sel(SUCtrl[1:0]),
    .en(SUCtrl[3]));
  Multiplexer #(.select(2), .enable("false")) multiplexer_13 (
    .in0(multiplexer_14_out), .in1(multiplexer_12_out), .in2(1'b0), .in3(multiplexer_12_out),
    .out(multiplexer_13_out), .sel(SUCtrl[2:1]));
  Multiplexer #(.select(2)) multiplexer_14 (
    .in0(X[0]), .in1(1'b0), .in2(X[1]), .in3(X[1]), .out(multiplexer_14_out), .sel(SUCtrl[1:0]),
    .en(SUCtrl[3]));
  Multiplexer #(.select(2), .enable("false")) multiplexer_15 (
    .in0(multiplexer_16_out), .in1(multiplexer_14_out), .in2(1'b0), .in3(multiplexer_14_out),
    .out(multiplexer_15_out), .sel(SUCtrl[2:1]));
  Multiplexer #(.select(2)) multiplexer_16 (
    .in0(1'b0), .in1(1'b0), .in2(X[0]), .in3(X[0]), .out(multiplexer_16_out), .sel(SUCtrl[1:0]),
    .en(SUCtrl[3]));
  not not_1 (not_1_out, SUCtrl[3]);
  and and_1 (and_1_out, not_1_out, X[6]);
  and and_2 (and_2_out, not_1_out, X[7]);
  or or_1 (R[7], multiplexer_1_out, and_2_out);
  or or_2 (R[6], multiplexer_3_out, and_1_out);
  or or_3 (R[5], multiplexer_6_out, and_3_out);
  and and_3 (and_3_out, not_1_out, X[5]);
  and and_4 (and_4_out, not_1_out, X[4]);
  and and_5 (and_5_out, not_1_out, X[3]);
  or or_4 (R[4], multiplexer_7_out, and_4_out);
  or or_5 (R[3], multiplexer_9_out, and_5_out);
  and and_6 (and_6_out, not_1_out, X[0]);
  and and_7 (and_7_out, not_1_out, X[2]);
  and and_8 (and_8_out, not_1_out, X[1]);
  or or_6 (R[2], multiplexer_11_out, and_7_out);
  or or_7 (R[2], multiplexer_13_out, and_8_out);
  or or_8 (R[0], multiplexer_15_out, and_6_out);
  not not_2 (not_2_out, 1'b0);
  not not_3 (not_3_out, R[0]);
  not not_4 (not_4_out, R[2]);
  not not_5 (not_5_out, R[2]);
  not not_6 (not_6_out, R[3]);
  not not_7 (not_7_out, R[4]);
  not not_8 (not_8_out, R[5]);
  not not_9 (not_9_out, R[6]);
  not not_10 (not_10_out, R[7]);
  and and_9 (ZF, not_2_out, not_3_out, not_4_out, not_5_out, not_6_out, not_7_out, not_8_out, not_9_out, not_10_out);
  xor xor_1 (Ouflw, X[7], R[7]);

  assign R[1] = R[2];
  assign SF = R[7];
endmodule
